// Logisim project Lab3.circ as structural Verilog: 4 circuits, main circuit Intro
module Intro (
  input  A,
  input  B,
  output P
);

  and and_1 (P, A, B);
endmodule

module _2_Bit_Parity (
  input  A,
  input  B,
  output P
);

  wire and_1_out, and_2_out, not_1_out, not_2_out;

  not not_1 (not_1_out, A);
  not not_2 (not_2_out, B);
  and and_1 (and_1_out, not_1_out, B);
  and and_2 (and_2_out, A, not_2_out);
  or or_1 (P, and_1_out, and_2_out);
endmodule

module DeMorgan1 (
  input  A,
  input  B,
  output P1,
  output P2
);

  wire not_1_out, not_2_out;

  not not_1 (not_1_out, A);
  not not_2 (not_2_out, B);
  nor nor_1 (P1, A, B);
  and and_1 (P2, not_1_out, not_2_out);
endmodule

module DeMorgan2 (
  input  A,
  input  B,
  output P1,
  output P2
);

  wire not_1_out, not_2_out;

  not not_1 (not_1_out, A);
  not not_2 (not_2_out, B);
  nand nand_1 (P1, A, B);
  or or_1 (P2, not_1_out, not_2_out);
endmodule
