// Logisim project Lab4.circ as structural Verilog: 2 circuits, main circuit Simplify 1
module Simplify_1 (
  input  A,
  input  B,
  input  C,
  input  D,
  output p
);

  wire and_1_out, and_2_out, and_3_out, not_1_out, not_2_out, or_1_out;

  not not_1 (not_1_out, A);
  not not_2 (not_2_out, C);
  and and_1 (and_1_out, not_1_out, not_2_out);
  and and_2 (and_2_out, B, C, D);
  and and_3 (and_3_out, A, not_2_out, D);
  or or_1 (or_1_out, and_2_out, and_3_out);
  or or_2 (p, and_1_out, or_1_out);
endmodule

module Simplify_2 (
  input  A,
  input  B,
  input  C,
  output P
);

  wire and_1_out, and_2_out, and_3_out, not_1_out, not_2_out, or_2_out;

  not not_1 (not_1_out, A);
  and and_1 (and_1_out, A, B);
  and and_2 (and_2_out, B, not_1_out, C);
  not not_2 (not_2_out, B);
  and and_3 (and_3_out, not_2_out, C, A);
  or or_1 (P, and_1_out, or_2_out);
  or or_2 (or_2_out, and_2_out, and_3_out);
endmodule
