// Logisim project Lab74BitAdder.circ as structural Verilog: 3 circuits, main circuit 4-Bit Adder
module Half_Adder (
  input  A,
  input  B,
  output Carry,
  output Sum
);

  and and_1 (Carry, A, B);
  xor xor_1 (Sum, A, B);
endmodule

module Full_Adder (
  input  A,
  input  B,
  input  Carry_In,
  output Carry_Out,
  output Sum
);

  wire Half_Adder_1_carry, Half_Adder_1_sum, Half_Adder_2_carry;

  Half_Adder Half_Adder_1 (.A(A), .B(B), .Carry(Half_Adder_1_carry), .Sum(Half_Adder_1_sum));
  or or_1 (Carry_Out, Half_Adder_1_carry, Half_Adder_2_carry);
  Half_Adder Half_Adder_2 (.A(Half_Adder_1_sum), .B(Carry_In), .Carry(Half_Adder_2_carry), .Sum(Sum));
endmodule

module _4_Bit_Adder (
  input  [3:0] _4_Bit_1,
  input  [3:0] _4_Bit_2,
  input  Carry_In,
  output Carry_out,
  output out_5,
  output out_6,
  output out_7,
  output out_8
);

  wire FA1_carry_out, FA2_carry_out, FA3_carry_out;

  Full_Adder FA1 (.A(_4_Bit_1[0]), .B(_4_Bit_2[0]), .Carry_In(Carry_In), .Carry_Out(FA1_carry_out), .Sum(out_8));
  Full_Adder FA2 (.A(_4_Bit_1[1]), .B(_4_Bit_2[1]), .Carry_In(FA1_carry_out), .Carry_Out(FA2_carry_out), .Sum(out_7));
  Full_Adder FA3 (.A(_4_Bit_1[2]), .B(_4_Bit_2[2]), .Carry_In(FA2_carry_out), .Carry_Out(FA3_carry_out), .Sum(out_6));
  Full_Adder FA4 (.A(_4_Bit_1[3]), .B(_4_Bit_2[3]), .Carry_In(FA3_carry_out), .Carry_Out(Carry_out), .Sum(out_5));
endmodule
