// Logisim project Lab7FullAdder.circ as structural Verilog: 2 circuits, main circuit Full Adder
module Half_Adder (
  input  A,
  input  B,
  output Carry,
  output Sum
);

  and and_1 (Carry, A, B);
  xor xor_1 (Sum, A, B);
endmodule

module Full_Adder (
  input  A,
  input  B,
  input  Carry_In,
  output Carry_Out,
  output Sum
);

  wire Half_Adder_1_carry, Half_Adder_1_sum, Half_Adder_2_carry;

  Half_Adder Half_Adder_1 (.A(A), .B(B), .Carry(Half_Adder_1_carry), .Sum(Half_Adder_1_sum));
  or or_1 (Carry_Out, Half_Adder_1_carry, Half_Adder_2_carry);
  Half_Adder Half_Adder_2 (.A(Half_Adder_1_sum), .B(Carry_In), .Carry(Half_Adder_2_carry), .Sum(Sum));
endmodule
