// Logisim project Lab7HalfAdder.circ as structural Verilog: 1 circuit, main circuit Half Adder
module Half_Adder (
  input  A,
  input  B,
  output Carry,
  output Sum
);

  and and_1 (Carry, A, B);
  xor xor_1 (Sum, A, B);
endmodule
