// Logisim project q2.circ as structural Verilog: 1 circuit, main circuit Simplify 1
module Simplify_1 (
  input  A,
  input  B,
  input  C,
  input  D,
  output p
);

  wire and_1_out, and_2_out, and_3_out, not_1_out, not_2_out, or_1_out;

  not not_1 (not_1_out, A);
  not not_2 (not_2_out, C);
  and and_1 (and_1_out, not_1_out, not_2_out);
  and and_2 (and_2_out, B, C, D);
  and and_3 (and_3_out, A, not_2_out, D);
  or or_1 (or_1_out, and_2_out, and_3_out);
  or or_2 (p, and_1_out, or_1_out);
endmodule
